// Logisim project first gates.circ as structural Verilog: 1 circuit, main circuit main
module main (
  input  in_1,
  input  in_2,
  input  in_3,
  input  in_4,
  input  in_5,
  input  in_6,
  output out_7,
  output out_8,
  output out_9
);

  wire not_1_out, or_1_out, xor_1_out;

  not not_1 (not_1_out, in_2);
  or or_1 (or_1_out, in_3, in_4);
  xor xor_1 (xor_1_out, in_5, in_6);
  xor xor_2 (out_7, in_1, not_1_out);
  and and_1 (out_8, or_1_out, in_4);
  xor xor_3 (out_9, in_5, xor_1_out);
endmodule
